# Fritzing sketch distance_led (saved by Fritzing 0.9.3b)
breadboards: 1

parts:
  Raspberry_Pi_1 = Raspberry Pi 3 [part_number=RPI-3-V1.2]
  パーツ1 = SRF05 Ultrasonic Rangefinder
  LED1 = LED - 5mm [color="Red (633nm)" package="5 mm [THT]"]
  R1 = Resistor [tolerance=±5% resistance=220 package=THT]

nets:
  N1: Raspberry_Pi_1.GPIO4, R1.Pin_1
  N2: Raspberry_Pi_1.GPIO21, パーツ1.Echo
  N3: Raspberry_Pi_1.GPIO20, パーツ1.Trig
  GND: Raspberry_Pi_1.GND, パーツ1.GND, LED1.cathode
  5V: Raspberry_Pi_1.5V, パーツ1.VCC
  N4: LED1.anode, R1.Pin_0
