# Fritzing sketch multi-lchika (saved by Fritzing 0.9.3b)
breadboards: 1

parts:
  Raspberry_Pi_1 = Raspberry Pi 3 [part_number=RPI-3-V1.2]
  LED1 = LED - 5mm [color="Red (633nm)" package="5 mm [THT]"]
  LED2 = LED - 5mm [color="Red (633nm)" package="5 mm [THT]"]
  LED3 = LED - 5mm [color="Red (633nm)" package="5 mm [THT]"]
  LED4 = LED - 5mm [color="Red (633nm)" package="5 mm [THT]"]
  LED5 = LED - 5mm [color="Red (633nm)" package="5 mm [THT]"]
  LED6 = LED - 5mm [color="Red (633nm)" package="5 mm [THT]"]
  LED7 = LED - 5mm [color="Red (633nm)" package="5 mm [THT]"]
  LED8 = LED - 5mm [color="Red (633nm)" package="5 mm [THT]"]
  LED9 = LED - 5mm [color="Red (633nm)" package="5 mm [THT]"]
  R1 = Resistor [tolerance=±5% resistance=220 package=THT]
  R2 = Resistor [tolerance=±5% resistance=220 package=THT]
  R3 = Resistor [tolerance=±5% resistance=220 package=THT]

nets:
  N1: Raspberry_Pi_1.GPIO13, LED7.cathode, LED8.cathode, LED9.cathode
  N2: Raspberry_Pi_1.GPIO19, LED1.anode, LED4.anode, LED6.cathode, LED7.anode, R1.Pin_0
  N3: Raspberry_Pi_1.GPIO26, LED1.cathode, LED2.cathode, LED3.cathode
  N4: Raspberry_Pi_1.GPIO21, LED3.anode, LED6.anode, R3.Pin_1
  N5: Raspberry_Pi_1.GPIO20, R2.Pin_1
  N6: Raspberry_Pi_1.GPIO16, R1.Pin_1
  N7: LED2.anode, LED5.anode, LED8.anode, R2.Pin_0
  N8: LED4.cathode, LED5.cathode
  N9: LED9.anode, R3.Pin_0
