# Fritzing sketch seg7 (saved by Fritzing 0.9.3b)
breadboards: 1

parts:
  DI1 = 7-Segment LED Display [package=THT]
  DI2 = 7-Segment LED Display [package=THT]
  Raspberry_Pi_1 = Raspberry Pi 3 [part_number=RPI-3-V1.2]
  R1 = Resistor [tolerance=±5% resistance=220 package=THT]
  R2 = Resistor [tolerance=±5% resistance=220 package=THT]
  R3 = Resistor [tolerance=±5% resistance=220 package=THT]
  R4 = Resistor [tolerance=±5% resistance=220 package=THT]
  R5 = Resistor [tolerance=±5% resistance=220 package=THT]
  R6 = Resistor [tolerance=±5% resistance=220 package=THT]
  R7 = Resistor [tolerance=±5% resistance=220 package=THT]
  R8 = Resistor [tolerance=±5% resistance=220 package=THT]

nets:
  N1: DI1.cathodeE, DI1.cathodeDP, DI2.cathodeE, R3.Pin_0
  N2: DI1.cathodeD, DI2.cathodeD, R4.Pin_0
  N3: DI1.commAnode#2, DI2.cathodeC, R5.Pin_0
  N4: DI1.cathodeC, DI2.cathodeDP, R8.Pin_0
  N5: DI1.cathodeB, DI2.cathodeG, Raspberry_Pi_1.GPIO21
  N6: DI1.cathodeA, DI2.cathodeB, R6.Pin_0
  N7: DI1.commAnode#7, DI2.cathodeA, R7.Pin_0
  N8: DI1.cathodeF, DI2.commAnode#2, R1.Pin_0
  N9: DI1.cathodeG, DI2.commAnode#7, R2.Pin_0
  N10: DI2.cathodeF, Raspberry_Pi_1.GPIO20
  N11: Raspberry_Pi_1.GPIO10, R8.Pin_1
  N12: Raspberry_Pi_1.GPIO9, R7.Pin_1
  N13: Raspberry_Pi_1.GPIO11, R6.Pin_1
  N14: Raspberry_Pi_1.GPIO5, R5.Pin_1
  N15: Raspberry_Pi_1.GPIO6, R4.Pin_1
  N16: Raspberry_Pi_1.GPIO13, R3.Pin_1
  N17: Raspberry_Pi_1.GPIO19, R2.Pin_1
  N18: Raspberry_Pi_1.GPIO26, R1.Pin_1
