# Fritzing sketch shiftregister (saved by Fritzing 0.9.3b)
breadboards: 1

parts:
  Raspberry_Pi_1 = Raspberry Pi 3 [part_number=RPI-3-V1.2]
  IC1 = SHIFT REGISTER [package=dil16]
  R1 = Resistor [tolerance=±5% resistance=220 package=THT]
  R2 = Resistor [tolerance=±5% resistance=220 package=THT]
  R4 = Resistor [tolerance=±5% resistance=220 package=THT]
  R6 = Resistor [tolerance=±5% resistance=220 package=THT]
  R8 = Resistor [tolerance=±5% resistance=220 package=THT]
  LED1 = LED - 5mm [color="Red (633nm)" package="5 mm [THT]"]
  LED2 = LED - 5mm [color="Red (633nm)" package="5 mm [THT]"]
  LED3 = LED - 5mm [color="Red (633nm)" package="5 mm [THT]"]
  R9 = Resistor [tolerance=±5% resistance=220 package=THT]
  R10 = Resistor [tolerance=±5% resistance=220 package=THT]
  R11 = Resistor [tolerance=±5% resistance=220 package=THT]
  LED4 = LED - 5mm [color="Red (633nm)" package="5 mm [THT]"]
  LED5 = LED - 5mm [color="Red (633nm)" package="5 mm [THT]"]
  LED6 = LED - 5mm [color="Red (633nm)" package="5 mm [THT]"]
  LED7 = LED - 5mm [color="Red (633nm)" package="5 mm [THT]"]
  LED8 = LED - 5mm [color="Red (633nm)" package="5 mm [THT]"]

nets:
  3V3: Raspberry_Pi_1.3v3, IC1.SCL, IC1.VCC
  GND: Raspberry_Pi_1.GND, IC1.GND, IC1.G, LED1.cathode, LED2.cathode, LED3.cathode, LED4.cathode, LED5.cathode, LED6.cathode, LED7.cathode, LED8.cathode
  N1: Raspberry_Pi_1.GPIO21, IC1.SER
  N2: Raspberry_Pi_1.GPIO20, IC1.RCK
  N3: Raspberry_Pi_1.GPIO12, IC1.SCK
  N4: IC1.QB, R10.Pin_0
  N5: IC1.QC, R9.Pin_0
  N6: IC1.QD, R1.Pin_0
  N7: IC1.QE, R2.Pin_0
  N8: IC1.QF, R4.Pin_0
  N9: IC1.QG, R6.Pin_0
  N10: IC1.QH, R8.Pin_0
  N11: IC1.QA, R11.Pin_0
  N12: R1.Pin_1, LED5.anode
  N13: R2.Pin_1, LED4.anode
  N14: R4.Pin_1, LED1.anode
  N15: R6.Pin_1, LED2.anode
  N16: R8.Pin_1, LED3.anode
  N17: R9.Pin_1, LED6.anode
  N18: R10.Pin_1, LED7.anode
  N19: R11.Pin_1, LED8.anode
