# Fritzing sketch shiftregister2 (saved by Fritzing 0.9.3b)
breadboards: 2

parts:
  Raspberry_Pi_1 = Raspberry Pi 3 [part_number=RPI-3-V1.2]
  IC1 = SHIFT REGISTER [package=dil16]
  R1 = Resistor [tolerance=±5% resistance=220 package=THT]
  R2 = Resistor [tolerance=±5% resistance=220 package=THT]
  R4 = Resistor [tolerance=±5% resistance=220 package=THT]
  R6 = Resistor [tolerance=±5% resistance=220 package=THT]
  R8 = Resistor [tolerance=±5% resistance=220 package=THT]
  LED1 = LED - 5mm [color="Red (633nm)" package="5 mm [THT]"]
  LED2 = LED - 5mm [color="Red (633nm)" package="5 mm [THT]"]
  LED3 = LED - 5mm [color="Red (633nm)" package="5 mm [THT]"]
  R9 = Resistor [tolerance=±5% resistance=220 package=THT]
  R10 = Resistor [tolerance=±5% resistance=220 package=THT]
  R11 = Resistor [tolerance=±5% resistance=220 package=THT]
  LED4 = LED - 5mm [color="Red (633nm)" package="5 mm [THT]"]
  LED5 = LED - 5mm [color="Red (633nm)" package="5 mm [THT]"]
  LED6 = LED - 5mm [color="Red (633nm)" package="5 mm [THT]"]
  LED7 = LED - 5mm [color="Red (633nm)" package="5 mm [THT]"]
  LED8 = LED - 5mm [color="Red (633nm)" package="5 mm [THT]"]
  IC2 = SHIFT REGISTER [package=dil16]
  LED11 = LED - 5mm [color="Red (633nm)" package="5 mm [THT]"]
  LED12 = LED - 5mm [color="Red (633nm)" package="5 mm [THT]"]
  LED13 = LED - 5mm [color="Red (633nm)" package="5 mm [THT]"]
  LED14 = LED - 5mm [color="Red (633nm)" package="5 mm [THT]"]
  LED15 = LED - 5mm [color="Red (633nm)" package="5 mm [THT]"]
  LED16 = LED - 5mm [color="Red (633nm)" package="5 mm [THT]"]
  LED17 = LED - 5mm [color="Red (633nm)" package="5 mm [THT]"]
  LED18 = LED - 5mm [color="Red (633nm)" package="5 mm [THT]"]
  R12 = Resistor [tolerance=±5% resistance=220 package=THT]
  R13 = Resistor [tolerance=±5% resistance=220 package=THT]
  R14 = Resistor [tolerance=±5% resistance=220 package=THT]
  R15 = Resistor [tolerance=±5% resistance=220 package=THT]
  R16 = Resistor [tolerance=±5% resistance=220 package=THT]
  R17 = Resistor [tolerance=±5% resistance=220 package=THT]
  R18 = Resistor [tolerance=±5% resistance=220 package=THT]
  R19 = Resistor [tolerance=±5% resistance=220 package=THT]

nets:
  VCC: Raspberry_Pi_1.3v3, IC1.SCL, IC1.VCC, IC2.SCL, IC2.VCC
  GND: Raspberry_Pi_1.GND, IC1.GND, IC1.G, LED1.cathode, LED2.cathode, LED3.cathode, LED4.cathode, LED5.cathode, LED6.cathode, LED7.cathode, LED8.cathode, IC2.GND, IC2.G, LED11.cathode, LED12.cathode, LED13.cathode, LED14.cathode, LED15.cathode, LED16.cathode, LED17.cathode, LED18.cathode
  N1: Raspberry_Pi_1.GPIO21, IC1.SER, IC2.SER
  N2: Raspberry_Pi_1.GPIO20, IC1.RCK, IC2.RCK
  N3: Raspberry_Pi_1.GPIO12, IC1.SCK, IC2.SCK
  N4: IC1.QB, R10.Pin_0
  N5: IC1.QC, R9.Pin_0
  N6: IC1.QD, R1.Pin_0
  N7: IC1.QE, R2.Pin_0
  N8: IC1.QF, R4.Pin_0
  N9: IC1.QG, R6.Pin_0
  N10: IC1.QH, R8.Pin_0
  N11: IC1.QH*, IC2.QH*
  N12: IC1.QA, R11.Pin_0
  N13: R1.Pin_1, LED5.anode
  N14: R2.Pin_1, LED4.anode
  N15: R4.Pin_1, LED1.anode
  N16: R6.Pin_1, LED2.anode
  N17: R8.Pin_1, LED3.anode
  N18: R9.Pin_1, LED6.anode
  N19: R10.Pin_1, LED7.anode
  N20: R11.Pin_1, LED8.anode
  N21: IC2.QB, R18.Pin_0
  N22: IC2.QC, R17.Pin_0
  N23: IC2.QD, R16.Pin_0
  N24: IC2.QE, R15.Pin_0
  N25: IC2.QF, R14.Pin_0
  N26: IC2.QG, R13.Pin_0
  N27: IC2.QH, R12.Pin_0
  N28: IC2.QA, R19.Pin_0
  N29: LED11.anode, R19.Pin_1
  N30: LED12.anode, R18.Pin_1
  N31: LED13.anode, R17.Pin_1
  N32: LED14.anode, R16.Pin_1
  N33: LED15.anode, R15.Pin_1
  N34: LED16.anode, R14.Pin_1
  N35: LED17.anode, R13.Pin_1
  N36: LED18.anode, R12.Pin_1
