# Fritzing sketch human-sensor (saved by Fritzing 0.9.3b)
breadboards: 1

parts:
  LED1 = LED - 5mm [color="Red (633nm)" package="5 mm [THT]"]
  R1 = Resistor [tolerance=±5% resistance=220 package=THT]
  Raspberry_Pi_1 = Raspberry Pi 3 [part_number=RPI-3-V1.2]
  part = HC-SR501 Body Sensor Module

nets:
  N1: LED1.cathode, R1.Pin_1
  N2: LED1.anode, Raspberry_Pi_1.GPIO24
  GND: R1.Pin_0, Raspberry_Pi_1.GND, part.GND
  N3: Raspberry_Pi_1.GPIO23, part.OUT
  5V: Raspberry_Pi_1.5V, part.VCC

custom parts:
  HC-SR501 Body Sensor Module: Pyroelectric Infrared PIR Motion Sensor Detector Module
