# Fritzing sketch fullcolorled (saved by Fritzing 0.9.3b)
breadboards: 1

parts:
  LED1 = RGB LED (com. cathode, rgb) [package="5 mm [THT]"]
  R1 = Resistor [tolerance=±5% resistance=220 package=THT]
  R2 = Resistor [tolerance=±5% resistance=220 package=THT]
  R3 = Resistor [tolerance=±5% resistance=220 package=THT]
  Raspberry_Pi_1 = Raspberry Pi 3 [part_number=RPI-3-V1.2]

nets:
  N1: LED1.red_anode, R1.Pin_0
  N2: LED1.common_cathode, R2.Pin_0
  N3: LED1.green_anode, Raspberry_Pi_1.GND
  N4: LED1.blue_anode, R3.Pin_0
  N5: R1.Pin_1, Raspberry_Pi_1.GPIO27
  N6: R2.Pin_1, Raspberry_Pi_1.GPIO17
  N7: R3.Pin_1, Raspberry_Pi_1.GPIO4
