# Fritzing sketch phototransistor (saved by Fritzing 0.9.3b)
breadboards: 1

parts:
  Raspberry_Pi_1 = Raspberry Pi 3 [part_number=RPI-3-V1.2]
  MCP1 = MCP3208
  Q1 = LTR-301 [package=ltr-301]
  R1 = Resistor [tolerance=±5% resistance=6.8k package=THT]

nets:
  N1: Raspberry_Pi_1.GPIO10, MCP1.DIN
  N2: Raspberry_Pi_1.GPIO9, MCP1.DOUT
  N3: Raspberry_Pi_1.GPIO11, MCP1.CLK
  N4: Raspberry_Pi_1.GND, MCP1.DGND, MCP1.AGND, R1.Pin_0
  N5: Raspberry_Pi_1.GPIO8, MCP1.CS/SHDN
  5V: Raspberry_Pi_1.5V, MCP1.Chan_0, MCP1.VREF, MCP1.VDD, Q1.E
  N6: Q1.C, R1.Pin_1
