# Fritzing sketch moter1 (saved by Fritzing 0.9.3b)
breadboards: 1

parts:
  Raspberry_Pi_Zero2 = Raspberry Pi Zero  # not connected
  U2 = TA7291P [package=HSIP10-P-2.54(THT)]
  M2 = DC Motor
  Raspberry_Pi_1 = Raspberry Pi 3 [part_number=RPI-3-V1.2]

nets:
  GND: U2.GND, Raspberry_Pi_1.GND
  N1: U2.OUT1, M2.pin_2
  N2: U2.Vref, Raspberry_Pi_1.GPIO18
  N3: U2.IN1, Raspberry_Pi_1.GPIO24
  N4: U2.IN2, Raspberry_Pi_1.GPIO25
  VCC: U2.Vcc, U2.Vs, Raspberry_Pi_1.5V
  N5: U2.OUT2, M2.pin_1

custom parts:
  TA7291P: The IC are Full-Bridge Driver. 4 modes available (CW / CCW / STOP / BRAKE) and PWM control. Output current:1.0 A (AVE.) 2.0 A (PEAK)
