# Fritzing sketch moter-joystick (saved by Fritzing 0.9.3b)
breadboards: 2

parts:
  Raspberry_Pi_Zero2 = Raspberry Pi Zero  # not connected
  U2 = TA7291P [package=HSIP10-P-2.54(THT)]
  M2 = DC Motor
  Raspberry_Pi_1 = Raspberry Pi 3 [part_number=RPI-3-V1.2]
  U3 = TA7291P [package=HSIP10-P-2.54(THT)]
  M3 = DC Motor
  VCC2 = 4 x AAA Battery Mount
  Onderdeel5 = Thumb Joystick
  MCP3 = MCP3208

nets:
  GND: U2.GND, Raspberry_Pi_1.GND, U3.GND, VCC2.-, Onderdeel5.GND, MCP3.DGND, MCP3.AGND
  N1: U2.OUT1, M3.pin_2
  N2: U2.Vref, Raspberry_Pi_1.GPIO18
  N3: U2.IN1, Raspberry_Pi_1.GPIO24
  N4: U2.IN2, Raspberry_Pi_1.GPIO25
  VCC: U2.Vcc, Raspberry_Pi_1.5V, U3.Vcc, Onderdeel5.VCC, MCP3.VREF, MCP3.VDD
  N5: U2.Vs, U3.Vs, VCC2.+
  N6: U2.9, M3.pin_1
  N7: M2.pin_1, U3.9
  N8: M2.pin_2, U3.OUT1
  N9: Raspberry_Pi_1.GPIO10, MCP3.DIN
  N10: Raspberry_Pi_1.GPIO9, MCP3.DOUT
  N11: Raspberry_Pi_1.GPIO11, MCP3.CLK
  N12: Raspberry_Pi_1.GPIO21, U3.IN2
  N13: Raspberry_Pi_1.GPIO20, U3.IN1
  N14: Raspberry_Pi_1.GPIO16, U3.Vref
  N15: Raspberry_Pi_1.GPIO8, MCP3.CS/SHDN
  N16: Onderdeel5.HORZ, MCP3.Chan_1
  N17: Onderdeel5.VERT, MCP3.Chan_0

custom parts:
  TA7291P: The IC are Full-Bridge Driver. 4 modes available (CW / CCW / STOP / BRAKE) and PWM control. Output current:1.0 A (AVE.) 2.0 A (PEAK)
